# Fritzing sketch BARU (saved by Fritzing 0.8.7b)

parts:
  M1 = ph-4502c [package=THT]
  Part1 = SRF05 Ultrasonic Rangefinder
  LCM1602_IIC1 = LCM1602 IIC [part_number="LCM1602 IIC" chip_label="LCM1602 IIC" package="DIP (Dual Inline) [THT]"]
  LCD1 = LCD screen
  U2 = LM2596 step down module
  4_Channel_Relay1 = 4 Channel Power Relay
  M2 = DC Motor
  M3 = DC Motor
  M4 = DC Motor
  M5 = DC Motor
  M6 = DC Motor
  KY-1 = Keyes Relay [package=THT]
  Power_plug1 = Power plug
  U3 = NodeMCU V1.0

nets:
  N1: M1.pin3, U3.A0
  GND: M1.pin4, M1.pin5, Part1.GND, LCM1602_IIC1.GND, U2.IN-, U2.OUT-, 4_Channel_Relay1.GND, M2.pin_2, M3.pin_2, M4.pin_2, M5.pin_2, M6.pin_2, KY-1.ground, Power_plug1.GND, U3.GND
  VCC: M1.pin6, LCM1602_IIC1.VCC, U2.OUT+, 4_Channel_Relay1.VCC, KY-1.power, U3.Vin
  VCC_2: Part1.VCC, U3.3V3
  N2: Part1.Trig, U3.D4
  N3: Part1.Echo, U3.D3
  VSS: LCM1602_IIC1.VSS, LCD1.VSS
  VDD: LCM1602_IIC1.VDD, LCD1.VDD
  N4: LCM1602_IIC1.V0, LCD1.V0
  N5: LCM1602_IIC1.RS, LCD1.RS
  N6: LCM1602_IIC1.RW, LCD1.R/W
  N7: LCM1602_IIC1.E, LCD1.E
  N8: LCM1602_IIC1.D0, LCD1.DB0
  N9: LCM1602_IIC1.D1, LCD1.DB1
  N10: LCM1602_IIC1.D2, LCD1.DB2
  N11: LCM1602_IIC1.D3, LCD1.DB3
  N12: LCM1602_IIC1.D4, LCD1.DB4
  N13: LCM1602_IIC1.D5, LCD1.DB5
  N14: LCM1602_IIC1.D6, LCD1.DB6
  N15: LCM1602_IIC1.D7, LCD1.DB7
  N16: LCM1602_IIC1.A, LCD1.LED+
  N17: LCM1602_IIC1.K, LCD1.LED-
  N18: LCM1602_IIC1.SDA, U3.D2
  N19: LCM1602_IIC1.SCL, U3.D1
  N20: U2.IN+, 4_Channel_Relay1.NO, KY-1.NO, Power_plug1.VCC
  N21: 4_Channel_Relay1.IN1, U3.D8
  N22: 4_Channel_Relay1.IN2, U3.D7
  N23: 4_Channel_Relay1.IN3, U3.D6
  N24: 4_Channel_Relay1.IN4, U3.D5
  N25: 4_Channel_Relay1.COM#17, M3.pin_1
  N26: 4_Channel_Relay1.COM#20, M5.pin_1
  N27: 4_Channel_Relay1.COM#23, M4.pin_1
  N28: 4_Channel_Relay1.COM#26, M6.pin_1
  N29: M2.pin_1, KY-1.C
  N30: KY-1.signal, U3.D0

notes:
  Pompa Buang Air
  Pompa Isi Air
  Pompa PH Down
  Pompa PH Up
  Pompa Utama
  Adaptor 12V

custom parts:
  ph-4502c: ph-4502c PH Meter.
  LCM1602 IIC: I2C-Module to use a 1602 or 2004 LCD on with the wire.h libory Serial LCD Modul
  LM2596 step down module: LM2596 DC-DC step down power supply module 3 A.
  4 Channel Power Relay: A 4 channel power relay. The module operates at 5V.
  Keyes Relay: The Keyes 5V relay module is suitable for SCM development, home appliance control. It uses a 5V~12V TIL control signal which can control DC / AC signal.
  NodeMCU V1.0: ESP8266 based NodeMCU
